# Fritzing sketch fritzing7segment (saved by Fritzing 0.9.4)
breadboards: 2

parts:
  Parça1 = Arduino Nano 33 BLE Sense
  7_Segment1 = 7 Segment Display
  S1 = Pushbutton [package="[SMD]"]
  S2 = Pushbutton [package="[SMD]"]
  R1 = Resistor [tolerance=±5% resistance=220 package=THT]
  R2 = Resistor [tolerance=±5% resistance=220 package=THT]
  R3 = Resistor [tolerance=±5% resistance=220 package=THT]
  R4 = Resistor [tolerance=±5% resistance=220 package=THT]
  R5 = Resistor [tolerance=±5% resistance=220 package=THT]
  R6 = Resistor [tolerance=±5% resistance=220 package=THT]
  R7 = Resistor [tolerance=±5% resistance=220 package=THT]

nets:
  N1: Parça1.GND, Parça1.A7, 7_Segment1.common_cathode
  N2: Parça1.D2, R5.Pin_1
  N3: Parça1.D3~, R6.Pin_1
  N4: Parça1.D4, R3.Pin_1
  N5: Parça1.D5~, R4.Pin_0
  N6: Parça1.D6~, R7.Pin_0
  N7: Parça1.D7, R1.Pin_0
  N8: Parça1.D8, R2.Pin_0
  N9: Parça1.D9~, S2.Pin_3, S2.Pin_4
  N10: Parça1.D10~, S1.Pin_3, S1.Pin_4
  N11: Parça1.D11/MOSI, Parça1.+5V
  N12: Parça1.3V3, S1.Pin_1, S1.Pin_2, S2.Pin_1, S2.Pin_2
  N13: 7_Segment1.Segment_E, R7.Pin_1
  N14: 7_Segment1.Segment_D, R4.Pin_1
  N15: 7_Segment1.Segment_C, R3.Pin_0
  N16: 7_Segment1.Segment_B, R6.Pin_0
  N17: 7_Segment1.Segment_A, R5.Pin_0
  N18: 7_Segment1.Segment_F, R1.Pin_1
  N19: 7_Segment1.Segment_G, R2.Pin_1

custom parts:
  Arduino Nano 33 BLE Sense: The Nano 33 BLE Sense (without headers) is Arduino’s 3.3V AI enabled board in the smallest available form factor: 45x18mm! The Arduino Nano 33 BLE Sense is a completely new board on a well-known form factor. It comes with a series of embedded sensors: 9 axis inertial sensor: what makes this board ideal for wearable devices humidity, and temperature sensor: to get highly accurate measurements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
